# Fritzing sketch buttons (saved by Fritzing 0.9.2b)
breadboards: 1

parts:
  S1 = Pushbutton [package="[THT]"]
  S2 = Pushbutton [package="[THT]"]
  S3 = Pushbutton [package="[THT]"]
  S4 = Pushbutton [package="[THT]"]
  S5 = Pushbutton [package="[THT]"]
  R1 = Resistor [tolerance=±5% resistance=4.7k package="2010 [SMD]"]
  R2 = Resistor [tolerance=±5% resistance=4.7k package="2010 [SMD]"]
  R3 = Resistor [tolerance=±5% resistance=4.7k package="2010 [SMD]"]
  R4 = Resistor [tolerance=±5% resistance=4.7k package="2010 [SMD]"]
  R5 = Resistor [tolerance=±5% resistance=4.7k package="2010 [SMD]"]
  R7 = Resistor [tolerance=±5% resistance=10k package="2010 [SMD]"]
  R8 = Resistor [tolerance=±5% resistance=10k package="2010 [SMD]"]
  R9 = Resistor [tolerance=±5% resistance=10k package="2010 [SMD]"]
  R10 = Resistor [tolerance=±5% resistance=10k package="2010 [SMD]"]
  R11 = Resistor [tolerance=±5% resistance=10k package="2010 [SMD]"]
  Parte1 = Arduino Nano (Rev3.0) (ICSP)

nets:
  N1: S1.Pin_1, S1.Pin_2, S2.Pin_1, S2.Pin_2, S3.Pin_1, S3.Pin_2, S4.Pin_1, S4.Pin_2, S5.Pin_1, S5.Pin_2, Parte1.5V
  N2: S1.Pin_3, S1.Pin_4, R1.Pin_0, R7.Pin_1
  N3: S2.Pin_3, S2.Pin_4, R1.Pin_1, R2.Pin_0, R8.Pin_1
  N4: S3.Pin_3, S3.Pin_4, R2.Pin_1, R3.Pin_0, R9.Pin_1
  N5: S4.Pin_3, S4.Pin_4, R3.Pin_1, R4.Pin_0, R10.Pin_1
  N6: S5.Pin_3, S5.Pin_4, R4.Pin_1, R5.Pin_0, R11.Pin_1
  N7: R5.Pin_1, Parte1.A0
  N8: R7.Pin_0, R8.Pin_0, R9.Pin_0, R10.Pin_0, R11.Pin_0, Parte1.GND
